# Fritzing sketch Schematic (saved by Fritzing 0.9.10b)

parts:
  Mod1 = KY-012 Active Buzzer Module [package="Breakout board"]
  Part1 = Arduino Uno (Rev3) - ICSP

nets:
  N1: Mod1.S, Part1.D7
  N2: Mod1.-, Part1.GND

custom parts:
  KY-012 Active Buzzer Module: Active Piezoelectric Buzzer Module KY-012, it produces single-tone sound when signal is high. (Special thanks to vanepp for fixing the PCB holes and other errors)
