# Fritzing sketch Schematic (saved by Fritzing 0.9.10b)

parts:
  Part1 = Arduino Uno (Rev3) - ICSP
  S1 = Pushbutton [package="[SMD]"]

nets:
  N1: Part1.D12/MISO, S1.Pin_2
  N2: Part1.GND, S1.Pin_4
