# Fritzing sketch Schematic (saved by Fritzing 0.9.10b)

parts:
  Part2 = Arduino Uno (Rev3) - ICSP
  Mod1 = KY-023 Dual Axis Joystick Module [package="Breakout board"]

nets:
  N1: Part2.A0, Mod1.VRy
  N2: Part2.A1, Mod1.VRx
  N3: Part2.D6_PWM, Mod1.SW
  5V: Part2.5V, Mod1.+5V
  GND: Part2.GND, Mod1.GND

custom parts:
  KY-023 Dual Axis Joystick Module: KY-023 Dual-Axis Joystick Module.
