# Fritzing sketch Schematic (saved by Fritzing 0.9.10b)

parts:
  LED2 = LED - 3mm [color="Red (633nm)" current=0.030 package="3 mm [THT]"]
  R1 = Resistor [tolerance=±5% resistance=220 package="2512 [SMD]"]
  Part1 = Arduino Uno (Rev3)

nets:
  N1: LED2.cathode, Part1.GND
  N2: R1.Pin_1, Part1.D12/MISO
