# Fritzing sketch Schematic (saved by Fritzing 0.9.10b)

parts:
  Mod1 = KY-027 Magic Light Cup Module [package="Breakout board"]
  Part1 = Arduino Uno (Rev3) - ICSP

nets:
  N1: Mod1.G, Part1.GND
  N2: Mod1.+, Part1.5V
  N3: Mod1.S, Part1.D7
  N4: Mod1.L, Part1.D6_PWM

custom parts:
  KY-027 Magic Light Cup Module: KY-0127 Magic Light Cup module is a set of two boards, each one has a led and a mercury tilt switch. Using PWM to drive the LEDs on each module you can achieve the effect of light being "magically" transferred from one module to the other when tilting them.
