# Fritzing sketch Schematic (saved by Fritzing 0.9.10b)

parts:
  R1 = Rotary Potentiometer (Large) [maximum_resistance=100kΩ knob_status=50% power=0.5W package=THT]
  Part1 = Arduino Uno (Rev3) - ICSP

nets:
  N1: R1.leg1, Part1.5V
  N2: R1.wiper, Part1.A0
  N3: R1.leg2, Part1.GND
