# Fritzing sketch Schematic (saved by Fritzing 0.9.10b)

parts:
  RE1 = KY-040 Rotary encoder [package=THT]
  Part1 = Arduino Uno (Rev3) - ICSP

nets:
  GND: RE1.GND, Part1.GND
  VCC: RE1.Vcc, Part1.5V
  N1: RE1.SW, Part1.D4
  N2: RE1.DT, Part1.D3_PWM
  N3: RE1.CLK, Part1.D2

custom parts:
  KY-040 Rotary encoder: KY-040 Rotary Encoder with switch on breakout borad from AZ Delivery
