# Fritzing sketch Schematic (saved by Fritzing 0.9.10b)

parts:
  LED2 = LED - 3mm [color="Red (633nm)" current=0.030 package="3 mm [THT]"]
  Part1 = Arduino Uno (Rev3)
  R2 = Resistor [tolerance=±5% power=0.25 resistance=470 package=THT]

nets:
  N1: LED2.cathode, Part1.GND
  N2: Part1.D12/MISO, R2.Pin_1
