# Fritzing sketch Schematic (saved by Fritzing 0.9.10b)

parts:
  Part1 = Arduino Uno (Rev3) - ICSP
  Mod1 = KY-009 Full Color RGB LED SMD Module [package="Breakout board"]

nets:
  N1: Part1.D3_PWM, Mod1.R
  N2: Part1.D5_PWM, Mod1.G
  N3: Part1.D6_PWM, Mod1.B
  N4: Part1.GND, Mod1.-

custom parts:
  KY-009 Full Color RGB LED SMD Module: KY-009 RGB full color LED Module, emits a range of colors by mixing red, green and blue light. The amount of each color is adjusted using PWM.
