# Fritzing sketch Schematic (saved by Fritzing 0.9.10b)

parts:
  SPI_SSD1 = OLED 0.95" 96x64 SPI SSD1331
  Part1 = Arduino Uno (Rev3) - ICSP

nets:
  VCC: SPI_SSD1.VCC, Part1.5V
  GND: SPI_SSD1.GND, Part1.GND
  N1: SPI_SSD1.DIN, Part1.ICSP_MOSI, Part1.D11_PWM/MOSI
  N2: SPI_SSD1.CLK, Part1.D13/SCK
  N3: SPI_SSD1.CS, Part1.D10_PWM/SS
  N4: SPI_SSD1.D/C, Part1.D8
  N5: SPI_SSD1.RES, Part1.D9_PWM
