# Fritzing sketch Schematic (saved by Fritzing 0.9.10b)
breadboards: 1

parts:
  Part1 = Arduino Uno (Rev3) - ICSP
  R1 = Temperature Sensor (Thermistor) [thermistor_type=NTC package=THT]
  R2 = Resistor [tolerance=±5% power=0.25 resistance=10k package=THT]

nets:
  N1: Part1.A0, R1.pin_0, R2.Pin_1
  N2: Part1.D2, R2.Pin_0
  N3: Part1.GND, R1.pin_1
